# Fritzing sketch CENG 317 Design[3850] (saved by Fritzing 0.9.3b)
circuit board: 6.53714cm x 3.20252cm
breadboards: 1

parts:
  TMP1 = TMP006 Temperature Sensor
  MCU1 = Raspberry Pi Zero

nets:
  N1: TMP1.VCC, MCU1.pin_1
  N2: TMP1.GND, MCU1.pin_6
  N3: TMP1.SDA, MCU1.pin_3
  N4: TMP1.SCL, MCU1.pin_5

notes:
  Jerreh Janneh

custom parts:
  TMP006 Temperature Sensor: TMP006 Contact-less Infrared Thermopile Sensor Breakout
